// Logisim project SAP-1_1607044_&_1607058.circ as structural Verilog: 20 circuits, main circuit Program_counter
module main (
  input  CLR,
  output [3:0] MSB,
  output [3:0] LSB,
  output out_4,
  output out_5,
  output out_6,
  output out_7,
  output out_8,
  output out_9,
  output out_10,
  output out_11
);

  wire CE, CLK, CLK_out, Cp, EA, EI, Ep, EU, HLT, LA, LB, LI, LM, LO, not_1_out, not_2_out, not_3_out,
       not_4_out, not_5_out, not_6_out, not_7_out, not_8_out, Sub;
  wire [3:0] mar_1_lsbout, register_1_lsbout, register_1_msbout, register_2_lsbout, register_2_msbout;
  wire [7:0] adder_subtracter_1_sum, register_4_lsbout;

  not not_1 (not_1_out, LM);
  not not_2 (not_2_out, CE);
  not not_3 (not_3_out, LI);
  Register register_1 (
    .MSBin(MSB), .LSBin(LSB), .MSBout(register_1_msbout), .LSBout(register_1_lsbout), .LOAD(not_3_out),
    .CLK(CLK), .CLR(CLR));
  Control_Sequencer control_sequencer_1 (
    .CLK(CLK), .CLR(CLR), .I7(register_1_msbout[3]), .I6(register_1_msbout[2]), .I5(register_1_msbout[1]),
    .I4(register_1_msbout[0]), .HLT(HLT), .CP(Cp), .EP(Ep), .Lm_bar(LM), .CE_bar(CE), .Li_bar(LI),
    .Ei_bar(EI), .La_bar(LA), .Ea(EA), .Su(Sub), .Eu(EU), .Lb_bar(LB), .Lo_bar(LO));
  Program_counter program_counter_1 (.Cp(Cp), .CLK(CLK), .CLR(CLR), .Ep(Ep), .out_5(LSB));
  MAR mar_1 (.LSBin(LSB), .LSBout(mar_1_lsbout), .LOAD(not_1_out), .CLK(CLK), .CLR(CLR));
  RAM #(.addrWidth(4)) ram_1 (.addr(mar_1_lsbout), .data({MSB, LSB}), .ld(not_2_out));  // open: sel, clk, clr
  assign LSB = not_4_out ? register_1_lsbout : 4'bz;  // Controlled_Buffer controlled_buffer_1
  not not_4 (not_4_out, EI);
  assign {MSB, LSB} = EA ? register_4_lsbout : 8'bz;  // Controlled_Buffer controlled_buffer_2
  assign {MSB, LSB} = EU ? adder_subtracter_1_sum : 8'bz;  // Controlled_Buffer controlled_buffer_3
  Register register_2 (
    .MSBin(MSB), .LSBin(LSB), .MSBout(register_2_msbout), .LSBout(register_2_lsbout), .LOAD(not_6_out),
    .CLK(CLK), .CLR(CLR));
  Register register_3 (
    .MSBin(MSB), .LSBin(LSB), .MSBout({out_11, out_10, out_9, out_8}), .LSBout({out_7, out_6, out_5, out_4}),
    .LOAD(not_5_out), .CLK(CLK), .CLR(CLR));
  not not_5 (not_5_out, LO);
  Adder_subtracter adder_subtracter_1 (
    .A(register_4_lsbout), .Sum(adder_subtracter_1_sum), .B({register_2_msbout, register_2_lsbout}), .SUB(Sub));
  not not_6 (not_6_out, LB);
  Register register_4 (
    .MSBin(MSB), .LSBin(LSB), .MSBout(register_4_lsbout[7:4]), .LSBout(register_4_lsbout[3:0]),
    .LOAD(not_7_out), .CLK(CLK), .CLR(CLR));
  not not_7 (not_7_out, LA);
  assign CLK = not_8_out ? CLK_out : 1'bz;  // Controlled_Buffer controlled_buffer_4
  Clock u_CLK (.out(CLK_out));
  not not_8 (not_8_out, HLT);
  Hex_Digit_Display hex_digit_display_1 (.value({out_11, out_10, out_9, out_8}));  // open: dp
  Hex_Digit_Display hex_digit_display_2 (.value({out_7, out_6, out_5, out_4}));  // open: dp

  // Notes on the sheet:
  //   RAM
  //   Control Sequencer
  //   Program Counter
  //   MAR
  //   IR
  //   Roll-1607044 && Roll - 1607058
  //   Adder-Subtracter
  //   Reg B
  //   Output Reg
  //   Accumulator
endmodule

module Program_counter (
  input  Cp,
  input  CLK,
  input  CLR,
  input  Ep,
  output [3:0] out_5
);

  wire j_k_ff_1_q, j_k_ff_2_q, j_k_ff_3_q, j_k_ff_4_q, not_1_out, not_2_out, not_3_out;

  J_K_Flip_Flop j_k_ff_1 (.J(Cp), .clk(CLK), .K(Cp), .Q(j_k_ff_1_q), .reset(CLR));  // open: Qn, preset, en
  assign out_5[0] = Ep ? j_k_ff_1_q : 1'bz;  // Controlled_Buffer controlled_buffer_1
  not not_1 (not_1_out, j_k_ff_1_q);
  J_K_Flip_Flop j_k_ff_2 (.J(Cp), .clk(not_1_out), .K(Cp), .Q(j_k_ff_2_q), .reset(CLR));  // open: Qn, preset, en
  not not_2 (not_2_out, j_k_ff_2_q);
  assign out_5[1] = Ep ? j_k_ff_2_q : 1'bz;  // Controlled_Buffer controlled_buffer_2
  J_K_Flip_Flop j_k_ff_3 (.J(Cp), .clk(not_2_out), .K(Cp), .Q(j_k_ff_3_q), .reset(CLR));  // open: Qn, preset, en
  assign out_5[2] = Ep ? j_k_ff_3_q : 1'bz;  // Controlled_Buffer controlled_buffer_3
  not not_3 (not_3_out, j_k_ff_3_q);
  J_K_Flip_Flop j_k_ff_4 (.J(Cp), .clk(not_3_out), .K(Cp), .Q(j_k_ff_4_q), .reset(CLR));  // open: Qn, preset, en
  assign out_5[3] = Ep ? j_k_ff_4_q : 1'bz;  // Controlled_Buffer controlled_buffer_4

  // Notes on the sheet:
  //   Roll-1607044
endmodule

module Single_Register (
  input  LOAD,
  input  Xi,
  input  CLK,
  input  CLR,
  input  Enable,
  output Yi
);

  wire and_1_out, and_2_out, d_ff_1_q, not_1_out, or_1_out;

  not not_1 (not_1_out, LOAD);
  and and_1 (and_1_out, d_ff_1_q, not_1_out);
  and and_2 (and_2_out, Xi, LOAD);
  or or_1 (or_1_out, and_1_out, and_2_out);
  D_Flip_Flop d_ff_1 (.clk(CLK), .D(or_1_out), .Q(d_ff_1_q), .reset(CLR));  // open: Qn, preset, en
  assign Yi = Enable ? d_ff_1_q : 1'bz;  // Controlled_Buffer controlled_buffer_1

  // Notes on the sheet:
  //   1607058
endmodule

module Register (
  input  [3:0] MSBin,
  input  [3:0] LSBin,
  input  LOAD,
  input  CLK,
  input  CLR,
  output [3:0] MSBout,
  output [3:0] LSBout
);

  Single_Register single_register_1 (.LOAD(LOAD), .Xi(MSBin[3]), .CLK(CLK), .CLR(CLR), .Enable(1'b1), .Yi(MSBout[3]));
  Single_Register single_register_2 (.LOAD(LOAD), .Xi(MSBin[2]), .CLK(CLK), .CLR(CLR), .Enable(1'b1), .Yi(MSBout[2]));
  Single_Register single_register_3 (.LOAD(LOAD), .Xi(MSBin[1]), .CLK(CLK), .CLR(CLR), .Enable(1'b1), .Yi(MSBout[1]));
  Single_Register single_register_4 (.LOAD(LOAD), .Xi(MSBin[0]), .CLK(CLK), .CLR(CLR), .Enable(1'b1), .Yi(MSBout[0]));
  Single_Register single_register_5 (.LOAD(LOAD), .Xi(LSBin[3]), .CLK(CLK), .CLR(CLR), .Enable(1'b1), .Yi(LSBout[3]));
  Single_Register single_register_6 (.LOAD(LOAD), .Xi(LSBin[2]), .CLK(CLK), .CLR(CLR), .Enable(1'b1), .Yi(LSBout[2]));
  Single_Register single_register_7 (.LOAD(LOAD), .Xi(LSBin[1]), .CLK(CLK), .CLR(CLR), .Enable(1'b1), .Yi(LSBout[1]));
  Single_Register single_register_8 (.LOAD(LOAD), .Xi(LSBin[0]), .CLK(CLK), .CLR(CLR), .Enable(1'b1), .Yi(LSBout[0]));

  // Notes on the sheet:
  //   1607058
endmodule

module Ring_Counter (
  input  CLK,
  input  CLR,
  output T1,
  output T2,
  output T3,
  output T4,
  output T5,
  output T6
);

  wire j_k_ff_1_q, j_k_ff_2_qn, j_k_ff_3_qn, j_k_ff_4_qn, j_k_ff_5_qn, j_k_ff_6_qn, not_1_out;

  not not_1 (not_1_out, CLK);
  J_K_Flip_Flop j_k_ff_1 (
    .J(j_k_ff_6_qn), .clk(not_1_out), .K(T6), .Q(j_k_ff_1_q), .Qn(T1), .reset(CLR));  // open: preset, en
  J_K_Flip_Flop j_k_ff_2 (
    .J(T1), .clk(not_1_out), .K(j_k_ff_1_q), .Q(T2), .Qn(j_k_ff_2_qn), .reset(CLR));  // open: preset, en
  J_K_Flip_Flop j_k_ff_3 (
    .J(T2), .clk(not_1_out), .K(j_k_ff_2_qn), .Q(T3), .Qn(j_k_ff_3_qn), .reset(CLR));  // open: preset, en
  J_K_Flip_Flop j_k_ff_4 (
    .J(T3), .clk(not_1_out), .K(j_k_ff_3_qn), .Q(T4), .Qn(j_k_ff_4_qn), .reset(CLR));  // open: preset, en
  J_K_Flip_Flop j_k_ff_5 (
    .J(T4), .clk(not_1_out), .K(j_k_ff_4_qn), .Q(T5), .Qn(j_k_ff_5_qn), .reset(CLR));  // open: preset, en
  J_K_Flip_Flop j_k_ff_6 (
    .J(T5), .clk(not_1_out), .K(j_k_ff_5_qn), .Q(T6), .Qn(j_k_ff_6_qn), .reset(CLR));  // open: preset, en

  // Notes on the sheet:
  //   1607058
endmodule

module MAR (
  input  [3:0] LSBin,
  input  LOAD,
  input  CLK,
  input  CLR,
  output [3:0] LSBout
);

  Single_Register single_register_1 (.LOAD(LOAD), .Xi(LSBin[3]), .CLK(CLK), .CLR(CLR), .Enable(1'b1), .Yi(LSBout[3]));
  Single_Register single_register_2 (.LOAD(LOAD), .Xi(LSBin[2]), .CLK(CLK), .CLR(CLR), .Enable(1'b1), .Yi(LSBout[2]));
  Single_Register single_register_3 (.LOAD(LOAD), .Xi(LSBin[1]), .CLK(CLK), .CLR(CLR), .Enable(1'b1), .Yi(LSBout[1]));
  Single_Register single_register_4 (.LOAD(LOAD), .Xi(LSBin[0]), .CLK(CLK), .CLR(CLR), .Enable(1'b1), .Yi(LSBout[0]));

  // Notes on the sheet:
  //   Roll-1607044
endmodule

module Adder_subtracter (
  input  [7:0] B,
  input  [7:0] A,
  input  SUB,
  output [7:0] Sum
);

  wire fa_1_c, fa_2_c, fa_3_c, fa_4_c, fa_5_c, fa_6_c, fa_7_c, fa_8_c, xor_1_out, xor_2_out, xor_3_out,
       xor_4_out, xor_5_out, xor_6_out, xor_7_out, xor_8_out;

  FA fa_1 (.X(A[7]), .Y(xor_1_out), .Z(fa_2_c), .S(Sum[7]), .C(fa_1_c));
  xor xor_1 (xor_1_out, B[7], SUB);
  xor xor_2 (xor_2_out, B[6], SUB);
  FA fa_2 (.X(A[6]), .Y(xor_2_out), .Z(fa_3_c), .S(Sum[6]), .C(fa_2_c));
  xor xor_3 (xor_3_out, B[5], SUB);
  FA fa_3 (.X(A[5]), .Y(xor_3_out), .Z(fa_4_c), .S(Sum[5]), .C(fa_3_c));
  xor xor_4 (xor_4_out, B[4], SUB);
  FA fa_4 (.X(A[4]), .Y(xor_4_out), .Z(fa_5_c), .S(Sum[4]), .C(fa_4_c));
  xor xor_5 (xor_5_out, B[3], SUB);
  FA fa_5 (.X(A[3]), .Y(xor_5_out), .Z(fa_6_c), .S(Sum[3]), .C(fa_5_c));
  xor xor_6 (xor_6_out, B[2], SUB);
  FA fa_6 (.X(A[2]), .Y(xor_6_out), .Z(fa_7_c), .S(Sum[2]), .C(fa_6_c));
  xor xor_7 (xor_7_out, B[1], SUB);
  FA fa_7 (.X(A[1]), .Y(xor_7_out), .Z(fa_8_c), .S(Sum[1]), .C(fa_7_c));
  FA fa_8 (.X(A[0]), .Y(xor_8_out), .Z(SUB), .S(Sum[0]), .C(fa_8_c));
  xor xor_8 (xor_8_out, B[0], SUB);

  // Notes on the sheet:
  //   Adder_subtracter
  //   Roll-1607044
endmodule

module C39 (
  input  _1,
  input  _4,
  input  _9,
  input  _10,
  input  _12,
  input  _13,
  output _3,
  output _6,
  output _8,
  output _11
);

  and and_1 (_3, _1, _10);
  and and_2 (_6, _4, _10);
  and and_3 (_11, _12, _13);
  and and_4 (_8, _9, _10);

  // Notes on the sheet:
  //   1607058
endmodule

module C40 (
  input  _1,
  input  _4,
  input  _5,
  input  _9,
  input  _12,
  input  _13,
  output _3,
  output _6,
  output _8,
  output _11
);

  and and_1 (_6, _4, _5);
  and and_2 (_3, _1, _5);
  and and_3 (_11, _12, _13);
  and and_4 (_8, _9, _13);

  // Notes on the sheet:
  //   1607058
endmodule

module C41 (
  input  _1,
  input  _2,
  input  _4,
  input  _5,
  input  _9,
  input  _12,
  input  _13,
  output _3,
  output _6,
  output _8,
  output _11
);

  and and_1 (_3, _1, _2);
  and and_2 (_6, _4, _5);
  and and_3 (_11, _12, _13);
  and and_4 (_8, _9, _13);

  // Notes on the sheet:
  //   1607058
endmodule

module C42 (
  input  _1,
  input  _2,
  input  _4,
  input  _5,
  input  _9,
  input  _12,
  input  _13,
  output _3,
  output _6,
  output _8,
  output _11
);

  and and_1 (_6, _4, _5);
  and and_2 (_3, _1, _2);
  and and_3 (_8, _9, _13);
  and and_4 (_11, _12, _13);

  // Notes on the sheet:
  //   1607058
endmodule

module C43 (
  input  _1,
  input  _4,
  input  _5,
  input  _9,
  input  _10,
  output _3,
  output _6,
  output _8
);

  and and_1 (_6, _4, _5);
  and and_2 (_3, _1, _5);
  and and_3 (_8, _9, _10);

  // Notes on the sheet:
  //   1607058
endmodule

module C44 (
  input  _1,
  input  _2,
  input  _4,
  input  _5,
  input  _9,
  input  _10,
  input  _12,
  input  _13,
  output _6,
  output _8
);

  or or_1 (_6, _1, _2, _4, _5);
  or or_2 (_8, _9, _10, _12, _13);

  // Notes on the sheet:
  //   1607058
endmodule

module C45 (
  input  _1,
  input  _2,
  input  _13,
  input  _3,
  input  _4,
  input  _5,
  output _12,
  output _6
);

  or or_1 (_12, _1, _2, _13);
  or or_2 (_6, _3, _4, _5);

  // Notes on the sheet:
  //   1607058
endmodule

module C46 (
  input  _1,
  input  _2,
  input  _4,
  input  _5,
  output _3,
  output _6
);

  or or_1 (_3, _1, _2);
  or or_2 (_6, _4, _5);

  // Notes on the sheet:
  //   1607058
endmodule

module Control_Sequencer (
  input  CLK,
  input  CLR,
  input  I7,
  input  I6,
  input  I5,
  input  I4,
  output HLT,
  output CP,
  output EP,
  output Lm_bar,
  output CE_bar,
  output Li_bar,
  output Ei_bar,
  output La_bar,
  output Ea,
  output Su,
  output Eu,
  output Lb_bar,
  output Lo_bar
);

  wire c39_1__3, c39_1__6, c39_1__8, c39_1__11, c40_1__3, c40_1__6, c40_1__8, c40_1__11, c41_1__3, c41_1__6,
       c41_1__8, c41_1__11, c42_1__8, c42_1__11, c43_1__3, c43_1__6, c43_1__8, c44_1__6, c44_1__8, c45_1__6,
       c45_1__12, c46_1__6, Instruction_Decoder_add, Instruction_Decoder_lda, Instruction_Decoder_out,
       Instruction_Decoder_sub, Ring_Counter_t3, Ring_Counter_t4, Ring_Counter_t5, Ring_Counter_t6;

  Instruction_Decoder Instruction_Decoder (
    .I7(I7), .I6(I6), .I5(I5), .I4(I4), .LDA(Instruction_Decoder_lda), .ADD(Instruction_Decoder_add),
    .SUB(Instruction_Decoder_sub), .OUT(Instruction_Decoder_out), .HLT(HLT));
  Ring_Counter Ring_Counter (
    .CLK(CLK), .CLR(CLR), .T1(EP), .T2(CP), .T3(Ring_Counter_t3), .T4(Ring_Counter_t4), .T5(Ring_Counter_t5),
    .T6(Ring_Counter_t6));
  C39 c39_1 (
    ._1(Instruction_Decoder_lda), ._4(Instruction_Decoder_add), ._9(Instruction_Decoder_sub),
    ._10(Ring_Counter_t4), ._12(Instruction_Decoder_lda), ._13(Ring_Counter_t5), ._3(c39_1__3),
    ._6(c39_1__6), ._8(c39_1__8), ._11(c39_1__11));
  C44 c44_1 (
    ._1(EP), ._2(c39_1__3), ._4(c39_1__6), ._5(c39_1__8), ._9(Ring_Counter_t3), ._10(c39_1__11),
    ._12(c40_1__3), ._13(c40_1__6), ._6(c44_1__6), ._8(c44_1__8));
  not not_1 (Lm_bar, c44_1__6);
  C40 c40_1 (
    ._1(Instruction_Decoder_add), ._4(Instruction_Decoder_sub), ._5(Ring_Counter_t5),
    ._9(Instruction_Decoder_lda), ._12(Instruction_Decoder_add), ._13(Ring_Counter_t4), ._3(c40_1__3),
    ._6(c40_1__6), ._8(c40_1__8), ._11(c40_1__11));
  not not_2 (Li_bar, Ring_Counter_t3);
  not not_3 (CE_bar, c44_1__8);
  C45 c45_1 (
    ._1(c40_1__8), ._2(c40_1__11), ._13(c41_1__3), ._3(c41_1__6), ._4(c41_1__8), ._5(c41_1__11),
    ._12(c45_1__12), ._6(c45_1__6));
  not not_4 (Ei_bar, c45_1__12);
  C41 c41_1 (
    ._1(Instruction_Decoder_sub), ._2(Ring_Counter_t4), ._4(Instruction_Decoder_lda), ._5(Ring_Counter_t5),
    ._9(Instruction_Decoder_add), ._12(Instruction_Decoder_sub), ._13(Ring_Counter_t6), ._3(c41_1__3),
    ._6(c41_1__6), ._8(c41_1__8), ._11(c41_1__11));
  not not_5 (La_bar, c45_1__6);
  C42 c42_1 (
    ._1(Instruction_Decoder_out), ._2(Ring_Counter_t4), ._4(Instruction_Decoder_sub), ._5(Ring_Counter_t6),
    ._9(Instruction_Decoder_add), ._12(Instruction_Decoder_sub), ._13(Ring_Counter_t6), ._3(Ea), ._6(Su),
    ._8(c42_1__8), ._11(c42_1__11));
  C46 c46_1 (._1(c42_1__8), ._2(c42_1__11), ._4(c43_1__3), ._5(c43_1__6), ._3(Eu), ._6(c46_1__6));
  C43 c43_1 (
    ._1(Instruction_Decoder_add), ._4(Instruction_Decoder_sub), ._5(Ring_Counter_t5),
    ._9(Instruction_Decoder_out), ._10(Ring_Counter_t4), ._3(c43_1__3), ._6(c43_1__6), ._8(c43_1__8));
  not not_6 (Lo_bar, c43_1__8);
  not not_7 (Lb_bar, c46_1__6);

  // Notes on the sheet:
  //   1607058
  //   T6
  //   T5
  //   T4
  //   T3
  //   T2
  //   T1
  //   LDA
  //   ADD
  //   SUB
  //   OUT
endmodule

module Instruction_Decoder (
  input  I7,
  input  I6,
  input  I5,
  input  I4,
  output LDA,
  output ADD,
  output SUB,
  output OUT,
  output HLT
);

  wire not_1_out, not_2_out, not_3_out, not_4_out;

  not not_1 (not_1_out, I7);
  not not_2 (not_2_out, I6);
  not not_3 (not_3_out, I5);
  not not_4 (not_4_out, I4);
  and C32 (LDA, not_1_out, not_2_out, not_3_out, not_4_out);
  and C32_2 (ADD, not_1_out, not_2_out, not_3_out, I4);
  and C33 (SUB, not_1_out, not_2_out, I5, not_4_out);
  and C33_2 (OUT, I7, I6, I5, not_4_out);
  and C32_3 (HLT, I7, I6, I5, I4);

  // Notes on the sheet:
  //   1607058
endmodule

module test_circuit (
  input  CLR,
  output [3:0] MSB,
  output [3:0] LSB,
  output out_4,
  output out_5,
  output out_6,
  output out_7,
  output out_8,
  output out_9,
  output out_10,
  output out_11
);

  wire CE, CLK, CLK_out, Cp, EA, EI, Ep, EU, HLT, LA, LB, LI, LM, LO, not_1_out, not_2_out, not_3_out,
       not_4_out, not_5_out, not_6_out, not_7_out, Sub;
  wire [3:0] register_1_lsbout, register_1_msbout, register_2_lsbout, undriven;
  wire [7:0] adder_subtracter_1_sum, register_4_lsbout;

  not not_1 (not_1_out, LM);
  not not_2 (not_2_out, CE);
  not not_3 (not_3_out, LI);
  Register register_1 (
    .MSBin(MSB), .LSBin(LSB), .MSBout(register_1_msbout), .LSBout(register_1_lsbout), .LOAD(not_3_out),
    .CLK(CLK), .CLR(CLR));
  Control_Sequencer control_sequencer_1 (
    .CLK(CLK), .CLR(CLR), .I7(register_1_msbout[3]), .I6(register_1_msbout[2]), .I5(register_1_msbout[1]),
    .I4(register_1_msbout[0]), .HLT(HLT), .CP(Cp), .EP(Ep), .Lm_bar(LM), .CE_bar(CE), .Li_bar(LI),
    .Ei_bar(EI), .La_bar(LA), .Ea(EA), .Su(Sub), .Eu(EU), .Lb_bar(LB), .Lo_bar(LO));
  Program_counter program_counter_1 (.Cp(Cp), .CLK(CLK), .CLR(CLR), .Ep(Ep), .out_5(LSB));
  MAR mar_1 (.LSBin(undriven), .LSBout(LSB), .LOAD(not_1_out), .CLK(CLK), .CLR(CLR));
  RAM #(.addrWidth(4)) ram_1 (.addr(undriven), .data({MSB, LSB}), .ld(not_2_out));  // open: sel, clk, clr
  assign LSB = EI ? register_1_lsbout : 4'bz;  // Controlled_Buffer controlled_buffer_1
  assign {MSB, LSB} = EA ? register_4_lsbout : 8'bz;  // Controlled_Buffer controlled_buffer_2
  assign {MSB, LSB} = EU ? adder_subtracter_1_sum : 8'bz;  // Controlled_Buffer controlled_buffer_3
  Register register_2 (
    .MSBin(MSB), .LSBin(LSB), .MSBout(LSB), .LSBout(register_2_lsbout), .LOAD(not_5_out), .CLK(CLK), .CLR(CLR));
  not not_4 (not_4_out, LO);
  Register register_3 (
    .MSBin(MSB), .LSBin(LSB), .MSBout({out_11, out_10, out_9, out_8}), .LSBout({out_7, out_6, out_5, out_4}),
    .LOAD(not_4_out), .CLK(CLK), .CLR(CLR));
  Adder_subtracter adder_subtracter_1 (
    .A(register_4_lsbout), .Sum(adder_subtracter_1_sum), .B({LSB, register_2_lsbout}), .SUB(Sub));
  not not_5 (not_5_out, LB);
  Register register_4 (
    .MSBin(MSB), .LSBin(LSB), .MSBout(register_4_lsbout[7:4]), .LSBout(register_4_lsbout[3:0]),
    .LOAD(not_6_out), .CLK(CLK), .CLR(CLR));
  not not_6 (not_6_out, LA);
  assign CLK = not_7_out ? CLK_out : 1'bz;  // Controlled_Buffer controlled_buffer_4
  Clock u_CLK (.out(CLK_out));
  not not_7 (not_7_out, HLT);
  Hex_Digit_Display hex_digit_display_1 (.value({out_11, out_10, out_9, out_8}));  // open: dp
  Hex_Digit_Display hex_digit_display_2 (.value({out_7, out_6, out_5, out_4}));  // open: dp

  // Notes on the sheet:
  //   RAM
  //   Control Sequencer
  //   Program Counter
  //   MAR
  //   IR
  //   Roll-1607044 && Roll - 1607058
  //   Adder-Subtracter
  //   Reg B
  //   Output Reg
  //   Accumulator
endmodule

module test_add_sub (
  input  [7:0] B,
  input  [7:0] A,
  input  SUB,
  output [7:0] Sum
);

  wire xor_1_out, xor_2_out, xor_3_out, xor_4_out, xor_5_out, xor_6_out, xor_7_out, xor_8_out;

  xor xor_1 (xor_1_out, B[7], SUB);
  xor xor_2 (xor_2_out, B[6], SUB);
  xor xor_3 (xor_3_out, B[5], SUB);
  xor xor_4 (xor_4_out, B[4], SUB);
  xor xor_5 (xor_5_out, B[3], SUB);
  xor xor_6 (xor_6_out, B[2], SUB);
  xor xor_7 (xor_7_out, B[1], SUB);
  xor xor_8 (xor_8_out, B[0], SUB);

  // Notes on the sheet:
  //   Adder_subtracter
  //   Roll-1607044
endmodule

module FA (
  input  X,
  input  Y,
  input  Z,
  output S,
  output C
);

  wire AND_2_out, AND_out, XOR_out;

  xor XOR (XOR_out, X, Y);
  and AND (AND_out, X, Y);
  and AND_2 (AND_2_out, XOR_out, Z);
  xor XOR_2 (S, XOR_out, Z);
  or or_1 (C, AND_2_out, AND_out);

  // Notes on the sheet:
  //   X
  //   Y
  //   X (XOR) Y
  //   XY
  //   Roll: 1607044
  //   Name : Sourav Mandol
  //   Z
  //   S = X (xor) Y (xor) Z
  //   C = Z(X xor Y) + XY
endmodule
